# Fritzing sketch ventilatore (saved by Fritzing 0.9.3b)
breadboards: 1

parts:
  Componente1 = Arduino Uno (Rev3)
  LCD1 = LCD screen
  M1 = DC Motor
  D1 = Zener Diode [part_number=1N4732A breakdown_voltage=3.6V package="300 mil [THT]"]
  R1 = Resistor [tolerance=±5% resistance=100 package=THT]
  Q1 = PNP-Transistor [package="TO92 [THT]"]
  U2 = POT [package=alps_pot]
  RHT1 = Humidity and Temperature Sensor RHT03

nets:
  N1: Componente1.D9_PWM, R1.Pin_1
  N2: Componente1.D11_PWM/MOSI, LCD1.E
  N3: Componente1.D12/MISO, LCD1.RS
  N4: Componente1.D13/SCK, RHT1.Vcc
  N5: Componente1.D2, LCD1.DB7
  N6: Componente1.D3_PWM, LCD1.DB6
  N7: Componente1.D4, LCD1.DB5
  N8: Componente1.D5_PWM, LCD1.DB4
  5V: Componente1.5V, LCD1.VDD, LCD1.LED+, M1.pin_1, D1.anode, U2.A, RHT1.Data-signal
  GND: Componente1.GND, LCD1.VSS, LCD1.R/W, LCD1.LED-, Q1.C, U2.E, RHT1.GND_1
  N9: LCD1.V0, U2.S
  N10: M1.pin_2, D1.cathode, Q1.E
  N11: R1.Pin_0, Q1.B

notes:
  il sensore di umidità ha solo 3 pin.
  1) pin analogico
  2) pin volt
  3) pin terra
